// Digital circuit ALU.dig as structural Verilog
module ALU (
  input  [31:0] rs1,
  input  [31:0] rs2,
  input  IS_1,
  input  f12,
  input  f13,
  input  f14,
  output u__gt,
  output u_lt,
  output u__eq,
  output gt,
  output lt,
  output V,
  output eq,
  output c_sub,
  output c_add,
  output [31:0] out
);

  wire [0:0] multiplexer_3_out;
  wire [31:0] add_out, and_out, multiplexer_1_out, multiplexer_2_out, or_out, sll_out, sra_out, srl_out,
       sub_out, xor_out;

  Add #(.Bits(32)) ADD (.a(rs1), .b(rs2), .c_i(1'b0), .s(add_out), .c_o(c_add));
  BarrelShifter #(.Bits(32)) SLL (.in(rs1), .shift({rs2[11:7], 1'b0}), .out(sll_out));
  Comparator #(.Signed("true"), .Bits(32)) SLTI (.a(rs1), .b(rs2), .gt(gt), .eq(eq), .lt(lt));
  Comparator #(.Bits(32)) SLTIU (.a(rs1), .b(rs2), .gt(u__gt), .eq(u__eq), .lt(u_lt));
  assign xor_out = rs1 ^ rs2;  // XOr xor_1, 32 bits wide
  BarrelShifter #(.Bits(32), .direction("right")) SRL (.in(rs1), .shift({rs2[11:7], 1'b0}), .out(srl_out));
  assign or_out = rs1 | rs2;  // Or or_1, 32 bits wide
  assign and_out = rs1 & rs2;  // And and_1, 32 bits wide
  Sub #(.Bits(32)) sub_1 (.a(rs1), .b(rs2), .c_i(1'b0), .s(sub_out), .c_o(c_sub));
  BarrelShifter #(.barrelShifterMode("arithmetic"), .Bits(32), .barrelSigned("true"), .direction("right")) sra (
    .in(rs1), .shift({rs2[11:7], 2'b00}), .out(sra_out));
  Multiplexer #(.Bits(32)) multiplexer_1 (.sel(eq), .in_0(32'h1), .in_1({32{1'b0}}), .out(multiplexer_1_out));
  Multiplexer #(.Bits(32)) multiplexer_2 (.sel(u__eq), .in_0(32'h1), .in_1({32{1'b0}}), .out(multiplexer_2_out));
  Multiplexer multiplexer_3 (.sel(IS_1), .in_0(1'b0), .in_1(1'b1), .out(multiplexer_3_out[0]));
  Multiplexer #(.Selector_Bits(4), .Bits(32)) multiplexer_4 (
    .sel({f14, f13, f12, multiplexer_3_out[0]}), .in_0(add_out), .in_1(sub_out), .in_2(xor_out),
    .in_3({32{1'b0}}), .in_4(multiplexer_1_out), .in_5({32{1'b0}}), .in_6(or_out), .in_7({32{1'b0}}),
    .in_8(sll_out), .in_9({32{1'b0}}), .in_10(srl_out), .in_11(sra_out), .in_12(multiplexer_2_out),
    .in_13({32{1'b0}}), .in_14(and_out), .in_15({32{1'b0}}), .out(out));

  assign V = gt;

  // Other names for the same wires on the sheet: barrel[31:0] = rs2; barrel_S[31:0] = rs2; shift[5:1] = rs2[11:7];
  //   shift_S[6:2] = rs2[11:7]; slti = eq; sltiu = u__eq
endmodule
