// Digital circuit JAL.dig as structural Verilog
module JAL (
  input  [31:0] PC,
  input  [31:0] imm,
  input  [31:0] rs1,
  input  sel,
  output jump
);

  wire multiplexer_1_out;

  Multiplexer multiplexer_1 (.sel(sel), .in_0(PC[0]), .in_1(rs1[0]), .out(multiplexer_1_out));
  Add add_1 (.a(multiplexer_1_out), .b(imm[0]), .s(jump));  // open: c_i, c_o
  // Pins of 1 and 32 bits meet at imm
  // Pins of 1 and 32 bits meet at PC
  // Pins of 1 and 32 bits meet at rs1
endmodule
