// Digital circuit branch.dig as structural Verilog
module branch (
  input  [31:0] PC,
  input  sel,
  input  [31:0] imm,
  output br
);

  wire multiplexer_1_out;

  Multiplexer multiplexer_1 (.sel(sel), .in_0(1'b0), .in_1(imm[0]), .out(multiplexer_1_out));
  Add add_1 (.a(PC[0]), .b(multiplexer_1_out), .s(br));  // open: c_i, c_o
  // Pins of 1 and 32 bits meet at PC
  // Pins of 1 and 3 bits meet at 3'b100
  // Pins of 1 and 32 bits meet at imm
endmodule
