// Digital circuit branch_evalk.dig as structural Verilog
module branch_evalk (
  input  Z,
  input  N,
  input  V,
  input  C,
  input  [2:0] f3,
  output branch_take
);

  wire not_1_out, not_2_out, not_3_out, xor_1_out;

  xor xor_1 (xor_1_out, N, V);
  not not_1 (not_1_out, Z);
  not not_2 (not_2_out, xor_1_out);
  not not_3 (not_3_out, C);
  Multiplexer #(.Selector_Bits(3)) multiplexer_1 (
    .sel(f3), .in_0(Z), .in_1(xor_1_out), .in_2(1'b0), .in_3(not_3_out), .in_4(not_1_out), .in_5(not_2_out),
    .in_6(1'b0), .in_7(C), .out(branch_take));
endmodule
