// Digital circuit cntrl.dig as structural Verilog
module cntrl (
  input  [31:0] i,
  input  clk,
  output R_str,
  output R_ld,
  output [1:0] WBs,
  output imm,
  output RgWr,
  output J,
  output br,
  output is_add,
  output alu_sel
);

  wire and_1_out, multiplexer_1_out;
  wire [2:0] counter_1_out;

  Comparator #(.Bits(8)) comparator_1 (.a({i[30], i[6:0]}), .b(8'h42), .eq(is_add));  // open: gt, lt
  Multiplexer multiplexer_1 (.sel(and_1_out), .in_0(1'b0), .in_1(1'b1), .out(multiplexer_1_out));
  Counter #(.Bits(3)) counter_1 (.en(1'b1), .C(clk), .clr(multiplexer_1_out), .out(counter_1_out));  // open: ovf
  and and_1 (and_1_out, counter_1_out[0], counter_1_out[2]);
  ROM #(.AddrBits(14), .Bits(8)) rom_1 (
    .A({i[30], i[14:12], i[6:0], counter_1_out}), .sel(1'b1), .D({RgWr, imm, R_ld, R_str, br, J, WBs}));

  assign alu_sel = i[30];

  // Other names for the same wires on the sheet: _0 = i[0]; opcode[6:0] = i[6:0]; _1 = i[1]; _2 = i[2]; _3 = i[3];
  //   _4 = i[4]; _5 = i[5]; _6 = i[6]; _7 = i[7]; _8 = i[8]; _9 = i[9]; _10 = i[10]; _11 = i[11]; _12 = i[12];
  //   _13 = i[13]; _14 = i[14]; _15 = i[15]; _16 = i[16]; _17 = i[17]; _18 = i[18]; _19 = i[19]; _20 = i[20];
  //   _21 = i[21]; _22 = i[22]; _23 = i[23]; _24 = i[24]; _25 = i[25]; _26 = i[26]; _27 = i[27]; _28 = i[28];
  //   _29 = i[29]; _30 = i[30]; _31 = i[31]
endmodule
