// Digital circuit datapath.dig as structural Verilog
module datapath (
  input  sel_rs2,
  input  clk
);

  wire imm, IR_q, multiplexer_1_out;
  wire [1:0] WBsel;
  wire [31:0] alu_1_p3, counter_1_out, imm_gen_1_p4, ramdualport_1_d, registerfile_1_da, registerfile_1_db,
       ROM_d;

  Counter #(.Bits(32), .isProgramCounter("true")) counter_1 (.C(clk), .out(counter_1_out));  // open: en, clr, ovf
  JAL jal_1 ();  // open: PC, imm, rs1, sel, jump
  RegisterFile #(.AddrBits(5), .Bits(32)) registerfile_1 (
    .Da(registerfile_1_da), .Db(registerfile_1_db));  // open: Din, we, Rw, C, Ra, Rb
  Multiplexer multiplexer_1 (.sel(sel_rs2), .in_0(imm), .in_1(registerfile_1_db[0]), .out(multiplexer_1_out));
  ROM #(.Bits(32)) ROM (.A(counter_1_out[1:0]), .D(ROM_d));  // open: sel
  branch branch_1 ();  // open: PC, sel, imm, br
  // ALU alu_1: pin names not known; wires that end beside it: registerfile_1_da, multiplexer_1_out, alu_1_p3
  flags flags_1 ();  // open: out, c_add, c_sub, _1r31, _2r31, add, N, C, V, Z
  Register IR (.D(ROM_d[0]), .C(clk), .Q(IR_q));  // open: en
  RAMDualPort ramdualport_1 (
    .A(alu_1_p3[1:0]), .Din(registerfile_1_db[0]), .D(ramdualport_1_d[0]));  // open: str, C, ld
  cntrl cntrl_1 ();  // open: i, clk, R_str, R_ld, WBs, imm, RgWr, J, br, is_add, alu_sel
  // imm_gen imm_gen_1: pin names not known; wires that end beside it: IR_q, IR_q, imm, imm_gen_1_p4
  Multiplexer #(.Selector_Bits(2), .Bits(32)) multiplexer_2 (
    .sel(WBsel), .in_0(ramdualport_1_d), .in_1(alu_1_p3), .out(imm_gen_1_p4));  // open: in_2, in_3
  // Pins of 2 and 32 bits meet at counter_1_out
  // Pins of 1 and 32 bits meet at ROM_d
  // Pins of 1 and 32 bits meet at registerfile_1_db
  // Pins of 2 and 32 bits meet at alu_1_p3
  // Pins of 1 and 32 bits meet at ramdualport_1_d
endmodule
