// Digital circuit flags.dig as structural Verilog
module flags (
  input  [31:0] out,
  input  c_add,
  input  c_sub,
  input  _1r31,
  input  _2r31,
  input  add,
  output N,
  output C,
  output V,
  output Z
);

  wire and_1_out;

  and and_1 (and_1_out, out[31], _1r31, _2r31);
  Comparator #(.Bits(32)) comparator_1 (.a(out), .b({32{1'b0}}), .eq(Z));  // open: gt, lt
  and and_2 (N, out[31], out[31]);
  and and_3 (C, c_add, c_sub);
  and and_4 (V, and_1_out, add);
endmodule
