// Digital circuit imm_gen.dig as structural Verilog
module imm_gen (
  input  [31:0] I,
  output [31:0] O
);

  wire and_1_out, and_2_out, and_3_out, and_4_out, and_5_out, and_6_out, dipswitch_1_out, dipswitch_2_out,
       dipswitch_3_out, dipswitch_4_out, dipswitch_5_out, dipswitch_6_out, dipswitch_7_out, dipswitch_8_out,
       dipswitch_9_out, dipswitch_10_out, dipswitch_11_out, dipswitch_12_out, dipswitch_13_out,
       dipswitch_14_out, dipswitch_15_out, dipswitch_16_out, dipswitch_17_out, dipswitch_18_out,
       dipswitch_19_out, dipswitch_21_out, dipswitch_22_out, dipswitch_23_out, dipswitch_24_out,
       dipswitch_25_out, dipswitch_26_out, dipswitch_27_out, dipswitch_28_out, dipswitch_30_out,
       dipswitch_31_out, dipswitch_32_out, dipswitch_33_out, dipswitch_34_out, dipswitch_35_out,
       dipswitch_37_out, dipswitch_38_out, dipswitch_39_out, dipswitch_40_out, dipswitch_41_out,
       dipswitch_42_out, dipswitch_43_out, dipswitch_44_out, dipswitch_46_out, not_1_out, not_2_out,
       not_3_out, not_4_out, not_5_out, not_6_out, xnor_1_out, xnor_2_out, xnor_3_out, xnor_4_out,
       xnor_5_out, xnor_6_out, xnor_7_out, xnor_8_out, xnor_9_out, xnor_10_out, xnor_11_out, xnor_12_out,
       xnor_13_out, xnor_14_out, xnor_15_out, xnor_16_out, xnor_17_out, xnor_18_out, xnor_19_out,
       xnor_20_out, xnor_21_out, xnor_22_out, xnor_23_out, xnor_24_out, xnor_25_out, xnor_26_out,
       xnor_27_out, xnor_28_out, xnor_29_out, xnor_30_out, xnor_31_out, xnor_32_out, xnor_33_out,
       xnor_34_out, xnor_35_out, xnor_36_out, xnor_37_out, xnor_38_out, xnor_39_out, xnor_40_out,
       xnor_41_out, xnor_42_out;
  wire [0:0] dipswitch_20_out, dipswitch_45_out;
  wire [11:11] dipswitch_29_out, dipswitch_36_out;
  wire [31:0] multiplexer_1_out, multiplexer_2_out, multiplexer_3_out, multiplexer_4_out, multiplexer_5_out,
       multiplexer_6_out;

  xnor xnor_1 (xnor_1_out, dipswitch_1_out, I[0]);
  DipSwitch dipswitch_1 (.out(dipswitch_1_out));
  xnor xnor_2 (xnor_2_out, dipswitch_2_out, I[1]);
  DipSwitch dipswitch_2 (.out(dipswitch_2_out));
  xnor xnor_3 (xnor_3_out, dipswitch_3_out, I[2]);
  DipSwitch #(.dipDefault("true")) dipswitch_3 (.out(dipswitch_3_out));
  xnor xnor_4 (xnor_4_out, dipswitch_4_out, I[3]);
  DipSwitch dipswitch_4 (.out(dipswitch_4_out));
  xnor xnor_5 (xnor_5_out, dipswitch_5_out, I[4]);
  DipSwitch dipswitch_5 (.out(dipswitch_5_out));
  and and_1 (and_1_out, xnor_7_out, xnor_6_out, xnor_5_out, xnor_4_out, xnor_3_out, xnor_2_out, xnor_1_out);
  xnor xnor_6 (xnor_6_out, dipswitch_6_out, I[5]);
  DipSwitch #(.dipDefault("true")) dipswitch_6 (.out(dipswitch_6_out));
  xnor xnor_7 (xnor_7_out, dipswitch_7_out, I[6]);
  DipSwitch #(.dipDefault("true")) dipswitch_7 (.out(dipswitch_7_out));
  not not_1 (not_1_out, and_1_out);
  Multiplexer #(.Bits(32)) multiplexer_1 (
    .sel(not_1_out), .in_0({{21{I[31]}}, I[30:20]}), .in_1({32{1'b0}}), .out(multiplexer_1_out));
  xnor xnor_8 (xnor_8_out, dipswitch_8_out, I[0]);
  DipSwitch #(.dipDefault("true")) dipswitch_8 (.out(dipswitch_8_out));
  xnor xnor_9 (xnor_9_out, dipswitch_9_out, I[1]);
  DipSwitch #(.dipDefault("true")) dipswitch_9 (.out(dipswitch_9_out));
  xnor xnor_10 (xnor_10_out, dipswitch_10_out, I[2]);
  DipSwitch dipswitch_10 (.out(dipswitch_10_out));
  xnor xnor_11 (xnor_11_out, dipswitch_11_out, I[3]);
  DipSwitch dipswitch_11 (.out(dipswitch_11_out));
  and and_2 (and_2_out, xnor_14_out, xnor_13_out, xnor_12_out, xnor_11_out, xnor_10_out, xnor_9_out, xnor_8_out);
  xnor xnor_12 (xnor_12_out, dipswitch_12_out, I[4]);
  DipSwitch dipswitch_12 (.out(dipswitch_12_out));
  xnor xnor_13 (xnor_13_out, dipswitch_13_out, I[5]);
  DipSwitch #(.dipDefault("true")) dipswitch_13 (.out(dipswitch_13_out));
  xnor xnor_14 (xnor_14_out, dipswitch_14_out, I[6]);
  DipSwitch dipswitch_14 (.out(dipswitch_14_out));
  not not_2 (not_2_out, and_2_out);
  Multiplexer #(.Bits(32)) multiplexer_2 (
    .sel(not_2_out), .in_0({{21{I[31]}}, I[30:25], I[11:7]}), .in_1({32{1'b0}}), .out(multiplexer_2_out));
  xnor xnor_15 (xnor_15_out, dipswitch_15_out, I[0]);
  DipSwitch #(.dipDefault("true")) dipswitch_15 (.out(dipswitch_15_out));
  xnor xnor_16 (xnor_16_out, dipswitch_16_out, I[1]);
  DipSwitch #(.dipDefault("true")) dipswitch_16 (.out(dipswitch_16_out));
  xnor xnor_17 (xnor_17_out, dipswitch_17_out, I[2]);
  DipSwitch dipswitch_17 (.out(dipswitch_17_out));
  xnor xnor_18 (xnor_18_out, dipswitch_18_out, I[3]);
  DipSwitch dipswitch_18 (.out(dipswitch_18_out));
  and and_3 (and_3_out, xnor_21_out, xnor_20_out, xnor_19_out, xnor_18_out, xnor_17_out, xnor_16_out, xnor_15_out);
  xnor xnor_19 (xnor_19_out, dipswitch_19_out, I[4]);
  DipSwitch dipswitch_19 (.out(dipswitch_19_out));
  DipSwitch dipswitch_20 (.out(dipswitch_20_out[0]));
  assign O = multiplexer_6_out | multiplexer_5_out | multiplexer_4_out | multiplexer_3_out | multiplexer_2_out | multiplexer_1_out;  // Or or_1, 32 bits wide
  xnor xnor_20 (xnor_20_out, dipswitch_21_out, I[5]);
  DipSwitch #(.dipDefault("true")) dipswitch_21 (.out(dipswitch_21_out));
  not not_3 (not_3_out, and_3_out);
  xnor xnor_21 (xnor_21_out, dipswitch_22_out, I[6]);
  DipSwitch #(.dipDefault("true")) dipswitch_22 (.out(dipswitch_22_out));
  Multiplexer #(.Bits(32)) multiplexer_3 (
    .sel(not_3_out), .in_0({{20{I[31]}}, I[7], I[30:25], I[11:8], dipswitch_20_out[0]}), .in_1({32{1'b0}}),
    .out(multiplexer_3_out));
  xnor xnor_22 (xnor_22_out, dipswitch_23_out, I[0]);
  DipSwitch #(.dipDefault("true")) dipswitch_23 (.out(dipswitch_23_out));
  xnor xnor_23 (xnor_23_out, dipswitch_24_out, I[1]);
  DipSwitch #(.dipDefault("true")) dipswitch_24 (.out(dipswitch_24_out));
  xnor xnor_24 (xnor_24_out, dipswitch_25_out, I[2]);
  DipSwitch dipswitch_25 (.out(dipswitch_25_out));
  xnor xnor_25 (xnor_25_out, dipswitch_26_out, I[3]);
  DipSwitch dipswitch_26 (.out(dipswitch_26_out));
  xnor xnor_26 (xnor_26_out, dipswitch_27_out, I[4]);
  DipSwitch #(.dipDefault("true")) dipswitch_27 (.out(dipswitch_27_out));
  and and_4 (and_4_out, xnor_28_out, xnor_27_out, xnor_26_out, xnor_25_out, xnor_24_out, xnor_23_out, xnor_22_out);
  xnor xnor_27 (xnor_27_out, dipswitch_28_out, I[5]);
  DipSwitch #(.dipDefault("true")) dipswitch_28 (.out(dipswitch_28_out));
  DipSwitch dipswitch_29 (.out(dipswitch_29_out[11]));
  xnor xnor_28 (xnor_28_out, dipswitch_30_out, I[6]);
  DipSwitch #(.dipDefault("true")) dipswitch_30 (.out(dipswitch_30_out));
  not not_4 (not_4_out, and_4_out);
  Multiplexer #(.Bits(32)) multiplexer_4 (
    .sel(not_4_out), .in_0({I[31:12], {12{dipswitch_29_out[11]}}}), .in_1({32{1'b0}}), .out(multiplexer_4_out));
  xnor xnor_29 (xnor_29_out, dipswitch_31_out, I[0]);
  DipSwitch #(.dipDefault("true")) dipswitch_31 (.out(dipswitch_31_out));
  xnor xnor_30 (xnor_30_out, dipswitch_32_out, I[1]);
  DipSwitch #(.dipDefault("true")) dipswitch_32 (.out(dipswitch_32_out));
  xnor xnor_31 (xnor_31_out, dipswitch_33_out, I[2]);
  DipSwitch #(.dipDefault("true")) dipswitch_33 (.out(dipswitch_33_out));
  xnor xnor_32 (xnor_32_out, dipswitch_34_out, I[3]);
  DipSwitch dipswitch_34 (.out(dipswitch_34_out));
  and and_5 (and_5_out, xnor_35_out, xnor_34_out, xnor_33_out, xnor_32_out, xnor_31_out, xnor_30_out, xnor_29_out);
  xnor xnor_33 (xnor_33_out, dipswitch_35_out, I[4]);
  DipSwitch #(.dipDefault("true")) dipswitch_35 (.out(dipswitch_35_out));
  DipSwitch dipswitch_36 (.out(dipswitch_36_out[11]));
  xnor xnor_34 (xnor_34_out, dipswitch_37_out, I[5]);
  DipSwitch #(.dipDefault("true")) dipswitch_37 (.out(dipswitch_37_out));
  xnor xnor_35 (xnor_35_out, dipswitch_38_out, I[6]);
  DipSwitch dipswitch_38 (.out(dipswitch_38_out));
  not not_5 (not_5_out, and_5_out);
  Multiplexer #(.Bits(32)) multiplexer_5 (
    .sel(not_5_out), .in_0({I[31:12], {12{dipswitch_36_out[11]}}}), .in_1({32{1'b0}}), .out(multiplexer_5_out));
  xnor xnor_36 (xnor_36_out, dipswitch_39_out, I[0]);
  DipSwitch #(.dipDefault("true")) dipswitch_39 (.out(dipswitch_39_out));
  xnor xnor_37 (xnor_37_out, dipswitch_40_out, I[1]);
  DipSwitch #(.dipDefault("true")) dipswitch_40 (.out(dipswitch_40_out));
  xnor xnor_38 (xnor_38_out, dipswitch_41_out, I[2]);
  DipSwitch dipswitch_41 (.out(dipswitch_41_out));
  xnor xnor_39 (xnor_39_out, dipswitch_42_out, I[3]);
  DipSwitch #(.dipDefault("true")) dipswitch_42 (.out(dipswitch_42_out));
  xnor xnor_40 (xnor_40_out, dipswitch_43_out, I[4]);
  DipSwitch #(.dipDefault("true")) dipswitch_43 (.out(dipswitch_43_out));
  and and_6 (and_6_out, xnor_42_out, xnor_41_out, xnor_40_out, xnor_39_out, xnor_38_out, xnor_37_out, xnor_36_out);
  xnor xnor_41 (xnor_41_out, dipswitch_44_out, I[5]);
  DipSwitch #(.dipDefault("true")) dipswitch_44 (.out(dipswitch_44_out));
  DipSwitch dipswitch_45 (.out(dipswitch_45_out[0]));
  xnor xnor_42 (xnor_42_out, dipswitch_46_out, I[6]);
  DipSwitch #(.dipDefault("true")) dipswitch_46 (.out(dipswitch_46_out));
  not not_6 (not_6_out, and_6_out);
  Multiplexer #(.Bits(32)) multiplexer_6 (
    .sel(not_6_out), .in_0({{12{I[31]}}, I[19:12], I[20], I[30:21], dipswitch_45_out[0]}), .in_1({32{1'b0}}),
    .out(multiplexer_6_out));

  // Other names for the same wires on the sheet: _0 = I[0]; _1 = I[1]; _2 = I[2]; _3 = I[3]; _4 = I[4]; _5 = I[5];
  //   _6 = I[6]; _7 = I[7]; _8 = I[8]; _9 = I[9]; _10 = I[10]; _11 = I[11]; _12 = I[12]; _13 = I[13]; _14 = I[14];
  //   _15 = I[15]; _16 = I[16]; _17 = I[17]; _18 = I[18]; _19 = I[19]; _20 = I[20]; _21 = I[21]; _22 = I[22];
  //   _23 = I[23]; _24 = I[24]; _25 = I[25]; _26 = I[26]; _27 = I[27]; _28 = I[28]; _29 = I[29]; _30 = I[30];
  //   _31 = I[31]

  // Notes on the sheet:
  //   I-TYPE, 111
  //   S-TYPE, 110
  //   B-TYPE, 101
  //   U1-TYPE, 100
  //   U2-TYPE, 011
  //   J-TYPE, 010
endmodule
